// Logisim project components.circ as structural Verilog: 14 circuits, main circuit main
module main (
);

  BitAnd Bitwise_AND ();  // open: A, B, S
  BitOr Bitwise_OR ();  // open: A, B, S
  BitNor Bitwise_NOR ();  // open: A, B, S
  NotZero Not_Zero ();  // open: A, A__0
  Decoder Decoder ();  // open: C, E, D
  Multiplexor Multiplexor ();  // open: A, B, S, M
  D_Latch Latch ();  // open: D, R, E, Q
  D_FlipFlop Flip_Flop ();  // open: D, R, C, Q
  RightShift Right_Shift ();  // open: A, i, o, S
  HalfAdder Half_Adder ();  // open: i, A, o, S
  IncDec Inc___Dec ();  // open: M, o, A, S
  AdcSbb Adc___Sbb ();  // open: M, i, A, B, S, o
  Comparator Comparator ();  // open: A, B, A_B, A_B_2, A_B_3
endmodule

module BitAnd (
  input  [7:0] A,
  input  [7:0] B,
  output [7:0] S
);

  and and_1 (S[0], A[0], B[0]);
  and and_2 (S[1], A[1], B[1]);
  and and_3 (S[2], A[2], B[2]);
  and and_4 (S[3], A[3], B[3]);
  and and_5 (S[4], A[4], B[4]);
  and and_6 (S[5], A[5], B[5]);
  and and_7 (S[6], A[6], B[6]);
  and and_8 (S[7], A[7], B[7]);
endmodule

module BitOr (
  input  [7:0] A,
  input  [7:0] B,
  output [7:0] S
);

  or or_1 (S[0], A[0], B[0]);
  or or_2 (S[1], A[1], B[1]);
  or or_3 (S[2], A[2], B[2]);
  or or_4 (S[3], A[3], B[3]);
  or or_5 (S[4], A[4], B[4]);
  or or_6 (S[5], A[5], B[5]);
  or or_7 (S[6], A[6], B[6]);
  or or_8 (S[7], A[7], B[7]);
endmodule

module BitNor (
  input  [7:0] A,
  input  [7:0] B,
  output [7:0] S
);

  nor nor_1 (S[0], A[0], B[0]);
  nor nor_2 (S[1], A[1], B[1]);
  nor nor_3 (S[2], A[2], B[2]);
  nor nor_4 (S[3], A[3], B[3]);
  nor nor_5 (S[4], A[4], B[4]);
  nor nor_6 (S[5], A[5], B[5]);
  nor nor_7 (S[6], A[6], B[6]);
  nor nor_8 (S[7], A[7], B[7]);
endmodule

module NotZero (
  input  [7:0] A,
  output A__0
);

  wire or_1_out, or_2_out, or_3_out, or_4_out, or_5_out, or_7_out;

  or or_1 (or_1_out, A[0], A[1]);
  or or_2 (or_2_out, A[2], A[3]);
  or or_3 (or_3_out, A[4], A[5]);
  or or_4 (or_4_out, A[6], A[7]);
  or or_5 (or_5_out, or_1_out, or_2_out);
  or or_6 (A__0, or_5_out, or_7_out);
  or or_7 (or_7_out, or_3_out, or_4_out);
endmodule

module RightShift (
  input  [7:0] A,
  input  i,
  output o,
  output [7:0] S
);


  assign o = A[0];
  assign S = {i, A[7:1]};
endmodule

module HalfAdder (
  input  i,
  input  [7:0] A,
  output [7:0] S,
  output o
);

  wire and_1_out, and_2_out, and_3_out, and_4_out, and_5_out, and_6_out, and_7_out;

  xor xor_1 (S[0], i, A[0]);
  and and_1 (and_1_out, i, A[0]);
  xor xor_2 (S[1], and_1_out, A[1]);
  and and_2 (and_2_out, and_1_out, A[1]);
  xor xor_3 (S[2], and_2_out, A[2]);
  and and_3 (and_3_out, and_2_out, A[2]);
  xor xor_4 (S[3], and_3_out, A[3]);
  and and_4 (and_4_out, and_3_out, A[3]);
  xor xor_5 (S[4], and_4_out, A[4]);
  and and_5 (and_5_out, and_4_out, A[4]);
  xor xor_6 (S[5], and_5_out, A[5]);
  and and_6 (and_6_out, and_5_out, A[5]);
  xor xor_7 (S[6], and_6_out, A[6]);
  and and_7 (and_7_out, and_6_out, A[6]);
  xor xor_8 (S[7], and_7_out, A[7]);
  and and_8 (o, and_7_out, A[7]);
endmodule

module IncDec (
  input  M,
  input  [7:0] A,
  output [7:0] S,
  output o
);

  wire and_1_out, and_2_out, and_3_out, and_4_out, and_5_out, and_6_out, and_7_out, xor_1_out, xor_2_out,
       xor_3_out, xor_4_out, xor_5_out, xor_6_out, xor_7_out, xor_8_out;

  xor xor_1 (xor_1_out, M, A[0]);
  xor xor_2 (xor_2_out, M, A[1]);
  xor xor_3 (xor_3_out, M, A[2]);
  xor xor_4 (xor_4_out, M, A[3]);
  xor xor_5 (xor_5_out, M, A[4]);
  xor xor_6 (xor_6_out, M, A[5]);
  xor xor_7 (xor_7_out, M, A[6]);
  xor xor_8 (xor_8_out, M, A[7]);
  and and_1 (and_1_out, 1'b0, xor_1_out);
  and and_2 (and_2_out, and_1_out, xor_2_out);
  and and_3 (and_3_out, and_2_out, xor_3_out);
  and and_4 (and_4_out, and_3_out, xor_4_out);
  and and_5 (and_5_out, and_4_out, xor_5_out);
  and and_6 (and_6_out, and_5_out, xor_6_out);
  and and_7 (and_7_out, and_6_out, xor_7_out);
  and and_8 (o, and_7_out, xor_8_out);
  xor xor_9 (S[0], 1'b0, A[0]);
  xor xor_10 (S[1], and_1_out, A[1]);
  xor xor_11 (S[2], and_2_out, A[2]);
  xor xor_12 (S[3], and_3_out, A[3]);
  xor xor_13 (S[4], and_4_out, A[4]);
  xor xor_14 (S[5], and_5_out, A[5]);
  xor xor_15 (S[6], and_6_out, A[6]);
  xor xor_16 (S[7], and_7_out, A[7]);
endmodule

module AdcSbb (
  input  M,
  input  i,
  input  [7:0] A,
  input  [7:0] B,
  output [7:0] S,
  output o
);

  wire and_1_out, and_2_out, and_3_out, and_4_out, and_5_out, and_6_out, and_7_out, and_8_out, and_9_out,
       and_10_out, and_11_out, and_12_out, and_13_out, and_14_out, and_15_out, and_16_out, or_1_out,
       or_2_out, or_3_out, or_4_out, or_5_out, or_6_out, or_7_out, xor_1_out, xor_2_out, xor_3_out,
       xor_4_out, xor_5_out, xor_6_out, xor_7_out, xor_8_out, xor_9_out, xor_10_out, xor_11_out, xor_12_out,
       xor_13_out, xor_14_out, xor_15_out, xor_16_out;

  xor xor_1 (xor_1_out, M, B[0]);
  xor xor_2 (xor_2_out, M, B[1]);
  xor xor_3 (xor_3_out, M, B[2]);
  xor xor_4 (xor_4_out, M, B[3]);
  xor xor_5 (xor_5_out, M, B[4]);
  xor xor_6 (xor_6_out, M, B[5]);
  xor xor_7 (xor_7_out, M, B[6]);
  xor xor_8 (xor_8_out, M, B[7]);
  xor xor_9 (xor_9_out, xor_1_out, A[0]);
  and and_1 (and_1_out, xor_1_out, A[0]);
  xor xor_10 (xor_10_out, xor_2_out, A[1]);
  and and_2 (and_2_out, xor_2_out, A[1]);
  xor xor_11 (xor_11_out, xor_3_out, A[2]);
  and and_3 (and_3_out, xor_3_out, A[2]);
  xor xor_12 (xor_12_out, xor_4_out, A[3]);
  and and_4 (and_4_out, xor_4_out, A[3]);
  xor xor_13 (xor_13_out, xor_5_out, A[4]);
  and and_5 (and_5_out, xor_5_out, A[4]);
  xor xor_14 (xor_14_out, xor_6_out, A[5]);
  and and_6 (and_6_out, xor_6_out, A[5]);
  xor xor_15 (xor_15_out, xor_7_out, A[6]);
  and and_7 (and_7_out, xor_7_out, A[6]);
  xor xor_16 (xor_16_out, xor_8_out, A[7]);
  and and_8 (and_8_out, xor_8_out, A[7]);
  xor xor_17 (S[0], xor_9_out, i);
  and and_9 (and_9_out, xor_9_out, i);
  or or_1 (or_1_out, and_9_out, and_1_out);
  xor xor_18 (S[1], xor_10_out, or_1_out);
  and and_10 (and_10_out, xor_10_out, or_1_out);
  or or_2 (or_2_out, and_10_out, and_2_out);
  xor xor_19 (S[2], xor_11_out, or_2_out);
  and and_11 (and_11_out, xor_11_out, or_2_out);
  or or_3 (or_3_out, and_11_out, and_3_out);
  xor xor_20 (S[3], xor_12_out, or_3_out);
  and and_12 (and_12_out, xor_12_out, or_3_out);
  or or_4 (or_4_out, and_12_out, and_4_out);
  xor xor_21 (S[4], xor_13_out, or_4_out);
  and and_13 (and_13_out, xor_13_out, or_4_out);
  or or_5 (or_5_out, and_13_out, and_5_out);
  xor xor_22 (S[5], xor_14_out, or_5_out);
  and and_14 (and_14_out, xor_14_out, or_5_out);
  or or_6 (or_6_out, and_14_out, and_6_out);
  xor xor_23 (S[6], xor_15_out, or_6_out);
  and and_15 (and_15_out, xor_15_out, or_6_out);
  or or_7 (or_7_out, and_15_out, and_7_out);
  xor xor_24 (S[7], xor_16_out, or_7_out);
  and and_16 (and_16_out, xor_16_out, or_7_out);
  or or_8 (o, and_16_out, and_8_out);
endmodule

module Comparator (
  input  [7:0] A,
  input  [7:0] B,
  output A_B,
  output A_B_2,
  output A_B_3
);

  wire and_1_out, and_2_out, and_3_out, and_4_out, and_5_out, and_6_out, and_7_out, and_8_out, and_9_out,
       and_10_out, and_11_out, and_12_out, and_13_out, and_14_out, and_16_out, and_17_out, and_18_out,
       and_19_out, and_20_out, and_21_out, and_22_out, not_1_out, not_2_out, not_3_out, not_4_out, not_5_out,
       not_6_out, not_7_out, not_8_out, or_1_out, or_2_out, or_3_out, or_4_out, or_5_out, or_6_out,
       xnor_1_out, xnor_2_out, xnor_3_out, xnor_4_out, xnor_5_out, xnor_6_out, xnor_7_out, xnor_8_out;

  and and_1 (and_1_out, A[7], not_1_out);
  not not_1 (not_1_out, B[7]);
  xnor xnor_1 (xnor_1_out, A[7], B[7]);
  and and_2 (and_2_out, A[6], not_2_out);
  not not_2 (not_2_out, B[6]);
  and and_3 (and_3_out, xnor_1_out, xnor_2_out);
  xnor xnor_2 (xnor_2_out, A[6], B[6]);
  and and_4 (and_4_out, A[5], not_3_out);
  not not_3 (not_3_out, B[5]);
  and and_5 (and_5_out, and_3_out, xnor_3_out);
  xnor xnor_3 (xnor_3_out, A[5], B[5]);
  and and_6 (and_6_out, A[4], not_4_out);
  not not_4 (not_4_out, B[4]);
  xnor xnor_4 (xnor_4_out, A[4], B[4]);
  and and_7 (and_7_out, and_5_out, xnor_4_out);
  and and_8 (and_8_out, A[3], not_5_out);
  not not_5 (not_5_out, B[3]);
  and and_9 (and_9_out, and_7_out, xnor_5_out);
  xnor xnor_5 (xnor_5_out, A[3], B[3]);
  and and_10 (and_10_out, A[2], not_6_out);
  not not_6 (not_6_out, B[2]);
  and and_11 (and_11_out, and_9_out, xnor_6_out);
  xnor xnor_6 (xnor_6_out, A[2], B[2]);
  and and_12 (and_12_out, A[1], not_7_out);
  not not_7 (not_7_out, B[1]);
  and and_13 (and_13_out, and_11_out, xnor_7_out);
  xnor xnor_7 (xnor_7_out, A[1], B[1]);
  and and_14 (and_14_out, A[0], not_8_out);
  not not_8 (not_8_out, B[0]);
  xnor xnor_8 (xnor_8_out, A[0], B[0]);
  and and_15 (A_B_3, and_13_out, xnor_8_out);
  and and_16 (and_16_out, xnor_1_out, and_2_out);
  and and_17 (and_17_out, and_3_out, and_4_out);
  and and_18 (and_18_out, and_5_out, and_6_out);
  and and_19 (and_19_out, and_7_out, and_8_out);
  and and_20 (and_20_out, and_9_out, and_10_out);
  and and_21 (and_21_out, and_11_out, and_12_out);
  and and_22 (and_22_out, and_13_out, and_14_out);
  or or_1 (or_1_out, and_1_out, and_16_out);
  or or_2 (or_2_out, or_1_out, or_3_out);
  or or_3 (or_3_out, and_17_out, and_18_out);
  or or_4 (or_4_out, and_19_out, and_20_out);
  or or_5 (or_5_out, or_4_out, or_6_out);
  or or_6 (or_6_out, and_21_out, and_22_out);
  or or_7 (A_B, or_2_out, or_5_out);
  nor nor_1 (A_B_2, A_B, A_B_3);
endmodule

// DCD
module Decoder (
  input  [2:0] C,
  input  E,
  output [7:0] D
);

  wire and_1_out, and_2_out, and_3_out, and_4_out, and_5_out, and_6_out, and_7_out, and_8_out, and_9_out,
       and_10_out, and_11_out, and_12_out, and_13_out, and_14_out, and_15_out, and_16_out, not_1_out,
       not_2_out, not_3_out;

  not not_1 (not_1_out, C[0]);
  not not_2 (not_2_out, C[1]);
  not not_3 (not_3_out, C[2]);
  and and_1 (and_1_out, not_1_out, not_2_out);
  and and_2 (and_2_out, and_1_out, not_3_out);
  and and_3 (and_3_out, C[0], not_2_out);
  and and_4 (and_4_out, and_3_out, not_3_out);
  and and_5 (and_5_out, not_1_out, C[1]);
  and and_6 (and_6_out, and_5_out, not_3_out);
  and and_7 (and_7_out, C[0], C[1]);
  and and_8 (and_8_out, and_7_out, not_3_out);
  and and_9 (and_9_out, not_1_out, not_2_out);
  and and_10 (and_10_out, and_9_out, C[2]);
  and and_11 (and_11_out, C[0], not_2_out);
  and and_12 (and_12_out, and_11_out, C[2]);
  and and_13 (and_13_out, not_1_out, C[1]);
  and and_14 (and_14_out, and_13_out, C[2]);
  and and_15 (and_15_out, C[0], C[1]);
  and and_16 (and_16_out, and_15_out, C[2]);
  and and_17 (D[0], and_2_out, E);
  and and_18 (D[1], and_4_out, E);
  and and_19 (D[2], and_6_out, E);
  and and_20 (D[3], and_8_out, E);
  and and_21 (D[4], and_10_out, E);
  and and_22 (D[5], and_12_out, E);
  and and_23 (D[6], and_14_out, E);
  and and_24 (D[7], and_16_out, E);
endmodule

// MUX
module Multiplexor (
  input  M,
  input  [7:0] A,
  input  [7:0] B,
  output [7:0] S
);

  wire and_1_out, and_2_out, and_3_out, and_4_out, and_5_out, and_6_out, and_7_out, and_8_out, and_9_out,
       and_10_out, and_11_out, and_12_out, and_13_out, and_14_out, and_15_out, and_16_out, not_1_out;

  not not_1 (not_1_out, M);
  and and_1 (and_1_out, M, B[0]);
  and and_2 (and_2_out, M, B[1]);
  and and_3 (and_3_out, M, B[2]);
  and and_4 (and_4_out, M, B[3]);
  and and_5 (and_5_out, M, B[4]);
  and and_6 (and_6_out, M, B[5]);
  and and_7 (and_7_out, M, B[6]);
  and and_8 (and_8_out, M, B[7]);
  and and_9 (and_9_out, not_1_out, A[0]);
  or or_1 (S[0], and_9_out, and_1_out);
  and and_10 (and_10_out, not_1_out, A[1]);
  or or_2 (S[1], and_10_out, and_2_out);
  and and_11 (and_11_out, not_1_out, A[2]);
  or or_3 (S[2], and_11_out, and_3_out);
  and and_12 (and_12_out, not_1_out, A[3]);
  or or_4 (S[3], and_12_out, and_4_out);
  and and_13 (and_13_out, not_1_out, A[4]);
  or or_5 (S[4], and_13_out, and_5_out);
  and and_14 (and_14_out, not_1_out, A[5]);
  or or_6 (S[5], and_14_out, and_6_out);
  and and_15 (and_15_out, not_1_out, A[6]);
  or or_7 (S[6], and_15_out, and_7_out);
  and and_16 (and_16_out, not_1_out, A[7]);
  or or_8 (S[7], and_16_out, and_8_out);
endmodule

// D-L
module D_Latch (
  input  [7:0] D,
  input  R,
  input  E,
  output [7:0] Q
);

  wire nand_1_out, nand_2_out, nand_3_out, nand_4_out, nand_5_out, nand_6_out, nand_7_out, nand_8_out,
       nand_9_out, nand_10_out, nand_11_out, nand_12_out, nand_13_out, nand_14_out, nand_15_out, nand_16_out,
       nand_18_out, nand_20_out, nand_22_out, nand_24_out, nand_26_out, nand_28_out, nand_30_out,
       nand_32_out, or_1_out;
  wire [7:0] controlled_buffer_1_out;

  assign controlled_buffer_1_out = R ? D : 8'bz;  // Controlled_Buffer controlled_buffer_1
  assign controlled_buffer_1_out = ~R ? {8{1'b0}} : 8'bz;  // Controlled_Buffer controlled_buffer_2
  nand nand_1 (nand_1_out, controlled_buffer_1_out[0], or_1_out);
  nand nand_2 (nand_2_out, nand_1_out, or_1_out);
  nand nand_3 (nand_3_out, controlled_buffer_1_out[1], or_1_out);
  nand nand_4 (nand_4_out, nand_3_out, or_1_out);
  nand nand_5 (nand_5_out, controlled_buffer_1_out[2], or_1_out);
  nand nand_6 (nand_6_out, nand_5_out, or_1_out);
  nand nand_7 (nand_7_out, controlled_buffer_1_out[3], or_1_out);
  nand nand_8 (nand_8_out, nand_7_out, or_1_out);
  nand nand_9 (nand_9_out, controlled_buffer_1_out[4], or_1_out);
  nand nand_10 (nand_10_out, nand_9_out, or_1_out);
  nand nand_11 (nand_11_out, controlled_buffer_1_out[5], or_1_out);
  nand nand_12 (nand_12_out, nand_11_out, or_1_out);
  nand nand_13 (nand_13_out, controlled_buffer_1_out[6], or_1_out);
  nand nand_14 (nand_14_out, nand_13_out, or_1_out);
  nand nand_15 (nand_15_out, controlled_buffer_1_out[7], or_1_out);
  nand nand_16 (nand_16_out, nand_15_out, or_1_out);
  or or_1 (or_1_out, ~R, E);  // OR_Gate
  nand nand_17 (Q[0], nand_1_out, nand_18_out);
  nand nand_18 (nand_18_out, Q[0], nand_2_out);
  nand nand_19 (Q[1], nand_3_out, nand_20_out);
  nand nand_20 (nand_20_out, Q[1], nand_4_out);
  nand nand_21 (Q[2], nand_5_out, nand_22_out);
  nand nand_22 (nand_22_out, Q[2], nand_6_out);
  nand nand_23 (Q[3], nand_7_out, nand_24_out);
  nand nand_24 (nand_24_out, Q[3], nand_8_out);
  nand nand_25 (Q[4], nand_9_out, nand_26_out);
  nand nand_26 (nand_26_out, Q[4], nand_10_out);
  nand nand_27 (Q[5], nand_11_out, nand_28_out);
  nand nand_28 (nand_28_out, Q[5], nand_12_out);
  nand nand_29 (Q[6], nand_13_out, nand_30_out);
  nand nand_30 (nand_30_out, Q[6], nand_14_out);
  nand nand_31 (Q[7], nand_15_out, nand_32_out);
  nand nand_32 (nand_32_out, Q[7], nand_16_out);
endmodule

// D-FF
module D_FlipFlop (
  input  [7:0] D,
  input  R,
  input  C,
  output [7:0] Q
);

  wire nand_1_out, nand_2_out, nand_3_out, nand_4_out, nand_5_out, nand_6_out, nand_7_out, nand_8_out,
       nand_9_out, nand_10_out, nand_11_out, nand_12_out, nand_13_out, nand_14_out, nand_15_out, nand_16_out,
       nand_17_out, nand_18_out, nand_19_out, nand_20_out, nand_21_out, nand_22_out, nand_23_out,
       nand_24_out, nand_25_out, nand_26_out, nand_27_out, nand_28_out, nand_29_out, nand_30_out,
       nand_31_out, nand_32_out, nand_33_out, nand_34_out, nand_35_out, nand_36_out, nand_37_out,
       nand_38_out, nand_39_out, nand_40_out, nand_41_out, nand_42_out, nand_43_out, nand_44_out,
       nand_45_out, nand_46_out, nand_47_out, nand_48_out, nand_49_out, nand_51_out, nand_53_out,
       nand_55_out, nand_57_out, nand_59_out, nand_61_out, nand_63_out, nand_65_out, or_1_out;
  wire [7:0] controlled_buffer_1_out;

  assign controlled_buffer_1_out = R ? D : 8'bz;  // Controlled_Buffer controlled_buffer_1
  assign controlled_buffer_1_out = ~R ? {8{1'b0}} : 8'bz;  // Controlled_Buffer controlled_buffer_2
  nand nand_1 (nand_1_out, R, C);
  nand nand_2 (nand_2_out, controlled_buffer_1_out[0], nand_1_out);
  nand nand_3 (nand_3_out, nand_2_out, nand_1_out);
  nand nand_4 (nand_4_out, controlled_buffer_1_out[1], nand_1_out);
  nand nand_5 (nand_5_out, nand_4_out, nand_1_out);
  nand nand_6 (nand_6_out, controlled_buffer_1_out[2], nand_1_out);
  nand nand_7 (nand_7_out, nand_6_out, nand_1_out);
  nand nand_8 (nand_8_out, controlled_buffer_1_out[3], nand_1_out);
  nand nand_9 (nand_9_out, nand_8_out, nand_1_out);
  nand nand_10 (nand_10_out, controlled_buffer_1_out[4], nand_1_out);
  nand nand_11 (nand_11_out, nand_10_out, nand_1_out);
  nand nand_12 (nand_12_out, controlled_buffer_1_out[5], nand_1_out);
  nand nand_13 (nand_13_out, nand_12_out, nand_1_out);
  nand nand_14 (nand_14_out, controlled_buffer_1_out[6], nand_1_out);
  nand nand_15 (nand_15_out, nand_14_out, nand_1_out);
  nand nand_16 (nand_16_out, controlled_buffer_1_out[7], nand_1_out);
  nand nand_17 (nand_17_out, nand_16_out, nand_1_out);
  nand nand_18 (nand_18_out, nand_2_out, nand_19_out);
  nand nand_19 (nand_19_out, nand_18_out, nand_3_out);
  nand nand_20 (nand_20_out, nand_4_out, nand_21_out);
  nand nand_21 (nand_21_out, nand_20_out, nand_5_out);
  nand nand_22 (nand_22_out, nand_6_out, nand_23_out);
  nand nand_23 (nand_23_out, nand_22_out, nand_7_out);
  nand nand_24 (nand_24_out, nand_8_out, nand_25_out);
  nand nand_25 (nand_25_out, nand_24_out, nand_9_out);
  nand nand_26 (nand_26_out, nand_10_out, nand_27_out);
  nand nand_27 (nand_27_out, nand_26_out, nand_11_out);
  nand nand_28 (nand_28_out, nand_12_out, nand_29_out);
  nand nand_29 (nand_29_out, nand_28_out, nand_13_out);
  nand nand_30 (nand_30_out, nand_14_out, nand_31_out);
  nand nand_31 (nand_31_out, nand_30_out, nand_15_out);
  nand nand_32 (nand_32_out, nand_16_out, nand_33_out);
  nand nand_33 (nand_33_out, nand_32_out, nand_17_out);
  or or_1 (or_1_out, ~R, C);  // OR_Gate
  nand nand_34 (nand_34_out, nand_18_out, or_1_out);
  nand nand_35 (nand_35_out, or_1_out, nand_19_out);
  nand nand_36 (nand_36_out, nand_20_out, or_1_out);
  nand nand_37 (nand_37_out, or_1_out, nand_21_out);
  nand nand_38 (nand_38_out, nand_22_out, or_1_out);
  nand nand_39 (nand_39_out, or_1_out, nand_23_out);
  nand nand_40 (nand_40_out, nand_24_out, or_1_out);
  nand nand_41 (nand_41_out, or_1_out, nand_25_out);
  nand nand_42 (nand_42_out, nand_26_out, or_1_out);
  nand nand_43 (nand_43_out, or_1_out, nand_27_out);
  nand nand_44 (nand_44_out, nand_28_out, or_1_out);
  nand nand_45 (nand_45_out, or_1_out, nand_29_out);
  nand nand_46 (nand_46_out, nand_30_out, or_1_out);
  nand nand_47 (nand_47_out, or_1_out, nand_31_out);
  nand nand_48 (nand_48_out, nand_32_out, or_1_out);
  nand nand_49 (nand_49_out, or_1_out, nand_33_out);
  nand nand_50 (Q[0], nand_34_out, nand_51_out);
  nand nand_51 (nand_51_out, Q[0], nand_35_out);
  nand nand_52 (Q[1], nand_36_out, nand_53_out);
  nand nand_53 (nand_53_out, Q[1], nand_37_out);
  nand nand_54 (Q[2], nand_38_out, nand_55_out);
  nand nand_55 (nand_55_out, Q[2], nand_39_out);
  nand nand_56 (Q[3], nand_40_out, nand_57_out);
  nand nand_57 (nand_57_out, Q[3], nand_41_out);
  nand nand_58 (Q[4], nand_42_out, nand_59_out);
  nand nand_59 (nand_59_out, Q[4], nand_43_out);
  nand nand_60 (Q[5], nand_44_out, nand_61_out);
  nand nand_61 (nand_61_out, Q[5], nand_45_out);
  nand nand_62 (Q[6], nand_46_out, nand_63_out);
  nand nand_63 (nand_63_out, Q[6], nand_47_out);
  nand nand_64 (Q[7], nand_48_out, nand_65_out);
  nand nand_65 (nand_65_out, Q[7], nand_49_out);
endmodule
