// Logisim project scheme.circ as structural Verilog: 11 circuits, main circuit MAIN
module MAIN (
  input  RST,
  input  INT
);

  wire central_contol_unit_1_ac, central_contol_unit_1_ar, central_contol_unit_1_as,
       central_contol_unit_1_ds, central_contol_unit_1_ef, central_contol_unit_1_er,
       central_contol_unit_1_ez, central_contol_unit_1_hlt, central_contol_unit_1_ic,
       central_contol_unit_1_is, central_contol_unit_1_lf, central_contol_unit_1_lg,
       central_contol_unit_1_lh, central_contol_unit_1_li, central_contol_unit_1_lm,
       central_contol_unit_1_lp, central_contol_unit_1_lr, central_contol_unit_1_lx,
       central_contol_unit_1_ly, central_contol_unit_1_mo, central_contol_unit_1_pi,
       central_contol_unit_1_po, central_contol_unit_1_rc, central_contol_unit_1_ri,
       central_contol_unit_1_ro, central_contol_unit_1_xt, CLK_out, general_purpose_registers_1_i,
       port_register_1_eb, port_register_1_ec, port_register_1_es, port_register_1_lb, port_register_1_lc,
       port_register_1_ls, port_register_1_se, program_counter_1_cof, stack_pointer_1_sof, step_counter_1_c;
  wire [2:0] step_counter_1_t;
  wire [7:0] stack_pointer_1_d_2;
  wire [15:0] memory_address_register_1_a_2, stack_pointer_1_a;

  Port_Register port_register_1 (
    .D(stack_pointer_1_d_2), .C(step_counter_1_c), .LP(central_contol_unit_1_lp), .SE(port_register_1_se),
    .EC(port_register_1_ec), .ES(port_register_1_es), .EB(port_register_1_eb), .LC(port_register_1_lc),
    .LS(port_register_1_ls), .LB(port_register_1_lb), .R(RST), .PI(central_contol_unit_1_pi),
    .PO(central_contol_unit_1_po));
  Stack_Pointer stack_pointer_1 (
    .LS(port_register_1_ls), .SE(port_register_1_se), .D(stack_pointer_1_d_2), .C(step_counter_1_c),
    .D_2(stack_pointer_1_d_2), .A(stack_pointer_1_a), .SOF(stack_pointer_1_sof),
    .DS(central_contol_unit_1_ds), .IS(central_contol_unit_1_is), .R(RST), .ES(port_register_1_es),
    .AS(central_contol_unit_1_as));
  Program_Counter program_counter_1 (
    .D(stack_pointer_1_d_2), .A(stack_pointer_1_a), .D_2(stack_pointer_1_d_2), .A_2(stack_pointer_1_a),
    .COF(program_counter_1_cof), .LC(port_register_1_lc), .SE(port_register_1_se),
    .RC(central_contol_unit_1_rc), .C(step_counter_1_c), .R(RST), .IC(central_contol_unit_1_ic),
    .EC(port_register_1_ec), .AC(central_contol_unit_1_ac));
  MEMORY memory_1 (
    .A(memory_address_register_1_a_2), .D(stack_pointer_1_d_2), .LB(port_register_1_lb),
    .SE(port_register_1_se), .C(step_counter_1_c), .D_2(stack_pointer_1_d_2), .R(RST),
    .RO(central_contol_unit_1_ro), .MO(central_contol_unit_1_mo), .EB(port_register_1_eb),
    .RI(central_contol_unit_1_ri));
  Memory_Address_Register memory_address_register_1 (
    .A(stack_pointer_1_a), .A_2(memory_address_register_1_a_2), .LM(central_contol_unit_1_lm),
    .C(step_counter_1_c), .R(RST));
  Instruction_Register instruction_register_1 (
    .D(stack_pointer_1_d_2), .O(stack_pointer_1_d_2), .LI(central_contol_unit_1_li), .C(step_counter_1_c),
    .R(RST));
  Clock CLK (.out(CLK_out));
  Step_Counter step_counter_1 (
    .HLT(central_contol_unit_1_hlt), .INT(INT), .COF(program_counter_1_cof), .SOF(stack_pointer_1_sof),
    .XT(central_contol_unit_1_xt), .R(RST), .C(step_counter_1_c), .T(step_counter_1_t), .CLK(CLK_out));
  General_Purpose_Registers general_purpose_registers_1 (
    .LF(central_contol_unit_1_lf), .LG(central_contol_unit_1_lg), .D(stack_pointer_1_d_2),
    .LH(central_contol_unit_1_lh), .O(stack_pointer_1_d_2), .C(step_counter_1_c),
    .LR(central_contol_unit_1_lr), .ER(central_contol_unit_1_er), .D_2(stack_pointer_1_d_2),
    .i(general_purpose_registers_1_i), .A(stack_pointer_1_a), .R(RST), .AR(central_contol_unit_1_ar));
  Arithmetic_Logic_Unit arithmetic_logic_unit_1 (
    .EF(central_contol_unit_1_ef), .EZ(central_contol_unit_1_ez), .O(stack_pointer_1_d_2),
    .D(stack_pointer_1_d_2), .LX(central_contol_unit_1_lx), .C(step_counter_1_c),
    .LY(central_contol_unit_1_ly), .R(RST), .i(general_purpose_registers_1_i), .D_2(stack_pointer_1_d_2));
  Central_Contol_Unit central_contol_unit_1 (
    .D(stack_pointer_1_d_2), .T(step_counter_1_t), .O(stack_pointer_1_d_2), .LH(central_contol_unit_1_lh),
    .LG(central_contol_unit_1_lg), .RC(central_contol_unit_1_rc), .IS(central_contol_unit_1_is),
    .HLT(central_contol_unit_1_hlt), .DS(central_contol_unit_1_ds), .LP(central_contol_unit_1_lp),
    .PI(central_contol_unit_1_pi), .PO(central_contol_unit_1_po), .LX(central_contol_unit_1_lx),
    .AS(central_contol_unit_1_as), .EF(central_contol_unit_1_ef), .LF(central_contol_unit_1_lf),
    .EZ(central_contol_unit_1_ez), .RI(central_contol_unit_1_ri), .RO(central_contol_unit_1_ro),
    .AR(central_contol_unit_1_ar), .AC(central_contol_unit_1_ac), .LM(central_contol_unit_1_lm),
    .LY(central_contol_unit_1_ly), .LR(central_contol_unit_1_lr), .LI(central_contol_unit_1_li),
    .MO(central_contol_unit_1_mo), .IC(central_contol_unit_1_ic), .ER(central_contol_unit_1_er),
    .XT(central_contol_unit_1_xt));
endmodule

// CCU
module Central_Contol_Unit (
  input  [7:0] D,
  input  [2:0] T,
  input  [7:0] O,
  output LH,
  output LG,
  output RC,
  output IS,
  output HLT,
  output DS,
  output LP,
  output PI,
  output PO,
  output LX,
  output AS,
  output EF,
  output LF,
  output EZ,
  output RI,
  output RO,
  output AR,
  output AC,
  output LM,
  output LY,
  output LR,
  output LI,
  output MO,
  output IC,
  output ER,
  output XT
);

  wire and_1_out, and_2_out, and_3_out, and_4_out, and_5_out, and_6_out, and_7_out, and_8_out, and_9_out,
       and_10_out, and_11_out, and_12_out, and_13_out, and_14_out, and_15_out, and_16_out, and_17_out,
       and_18_out, and_19_out, and_20_out, and_21_out, and_22_out, and_23_out, and_24_out, and_25_out,
       and_26_out, and_27_out, and_28_out, and_29_out, and_30_out, and_31_out, and_32_out, and_33_out,
       and_34_out, and_35_out, and_36_out, and_37_out, and_38_out, and_39_out, and_40_out, and_41_out,
       and_42_out, and_43_out, and_44_out, and_45_out, and_46_out, and_47_out, and_48_out, and_49_out,
       and_50_out, and_51_out, and_52_out, and_53_out, and_63_out, and_64_out, and_65_out, and_66_out,
       and_68_out, and_69_out, and_70_out, and_71_out, and_73_out, and_74_out, nor_1_out, nor_2_out,
       not_1_out, not_2_out, not_3_out, not_4_out, not_5_out, not_6_out, not_7_out, not_8_out, not_9_out,
       not_10_out, not_11_out, or_1_out, or_2_out, or_3_out, or_4_out, or_5_out, or_6_out, or_7_out,
       or_8_out, or_9_out, or_10_out, or_11_out, or_12_out, or_15_out, or_17_out, or_19_out, or_20_out,
       or_21_out, or_25_out, or_26_out, or_27_out, or_28_out, or_29_out, or_30_out, or_31_out, or_32_out,
       or_34_out, or_35_out;

  or or_1 (or_1_out, D[0], D[1], D[2], D[3], D[4], D[5], D[6], D[7]);
  not not_1 (not_1_out, O[5]);
  not not_2 (not_2_out, O[6]);
  not not_3 (not_3_out, O[7]);
  not not_4 (not_4_out, T[1]);
  not not_5 (not_5_out, T[2]);
  not not_6 (not_6_out, O[3]);
  not not_7 (not_7_out, O[4]);
  not not_8 (not_8_out, T[0]);
  and and_1 (and_1_out, T[1], T[2]);
  and and_2 (and_2_out, T[1], not_5_out);
  and and_3 (and_3_out, not_4_out, T[2]);
  and and_4 (and_4_out, O[5], not_7_out);
  and and_5 (and_5_out, not_1_out, O[4]);
  and and_6 (and_6_out, O[6], not_3_out);
  and and_7 (and_7_out, O[4], O[5]);
  and and_8 (and_8_out, not_2_out, not_3_out);
  and and_9 (and_9_out, not_2_out, O[7]);
  and and_10 (and_10_out, not_7_out, not_1_out);
  and and_11 (and_11_out, not_4_out, not_5_out);
  and and_12 (and_12_out, T[0], and_1_out);
  and and_13 (and_13_out, and_1_out, not_8_out);
  and and_14 (and_14_out, and_2_out, not_8_out);
  and and_15 (and_15_out, and_2_out, T[0]);
  and and_16 (and_16_out, and_3_out, T[0]);
  and and_17 (and_17_out, and_3_out, not_8_out);
  or or_2 (or_2_out, and_4_out, and_5_out);
  and and_18 (and_18_out, not_8_out, and_11_out);
  and and_19 (and_19_out, and_11_out, T[0]);
  and and_20 (and_20_out, and_17_out, not_6_out);
  and and_21 (and_21_out, and_16_out, not_6_out);
  and and_22 (and_22_out, and_17_out, O[3]);
  and and_23 (and_23_out, O[3], and_13_out);
  and and_24 (and_24_out, and_13_out, not_6_out);
  and and_25 (and_25_out, and_14_out, not_6_out);
  and and_26 (and_26_out, and_15_out, O[3]);
  and and_27 (and_27_out, and_15_out, not_6_out);
  and and_28 (and_28_out, O[3], and_16_out);
  and and_29 (and_29_out, and_17_out, and_6_out);
  and and_30 (and_30_out, or_2_out, and_8_out);
  and and_31 (and_31_out, and_6_out, and_7_out);
  and and_32 (and_32_out, and_7_out, and_8_out);
  and and_33 (and_33_out, and_10_out, and_9_out);
  and and_34 (and_34_out, and_6_out, and_10_out);
  and and_35 (and_35_out, or_2_out, and_6_out);
  and and_36 (and_36_out, and_8_out, and_10_out);
  and and_37 (and_37_out, and_5_out, and_9_out);
  or or_3 (or_3_out, and_21_out, and_22_out);
  or or_4 (or_4_out, and_22_out, and_25_out);
  and and_38 (and_38_out, O[7], and_20_out);
  or or_5 (or_5_out, and_20_out, and_26_out);
  not not_9 (not_9_out, and_33_out);
  not not_10 (not_10_out, and_37_out);
  and and_39 (and_39_out, and_26_out, and_32_out);
  and and_40 (and_40_out, and_25_out, and_36_out);
  and and_41 (and_41_out, not_9_out, O[7]);
  and and_42 (and_42_out, and_37_out, or_3_out);
  and and_43 (and_43_out, O[7], or_3_out);
  and and_44 (and_44_out, and_43_out, not_10_out);
  and and_45 (and_45_out, and_30_out, and_27_out);
  and and_46 (and_46_out, and_17_out, and_36_out);
  and and_47 (and_47_out, and_25_out, and_30_out);
  and and_48 (and_48_out, and_34_out, and_15_out);
  and and_49 (and_49_out, and_32_out, or_4_out);
  or or_6 (or_6_out, and_25_out, and_26_out);
  or or_7 (or_7_out, and_27_out, and_28_out);
  and and_50 (and_50_out, and_34_out, and_17_out);
  or or_8 (or_8_out, and_40_out, and_41_out);
  and and_51 (and_51_out, and_28_out, O[7]);
  or or_9 (or_9_out, and_42_out, and_24_out);
  and and_52 (and_52_out, and_28_out, and_32_out);
  or or_10 (or_10_out, and_44_out, and_46_out);
  or or_11 (or_11_out, and_45_out, and_12_out);
  or or_12 (or_12_out, and_23_out, and_47_out);
  or or_13 (AS, and_49_out, and_48_out);
  and and_53 (and_53_out, or_1_out, or_6_out);
  and and_54 (LH, and_26_out, and_30_out);
  and and_55 (LG, and_28_out, and_30_out);
  and and_56 (RC, and_53_out, and_31_out);
  and and_57 (IS, or_7_out, and_32_out);
  and and_58 (HLT, and_53_out, and_33_out);
  and and_59 (DS, and_14_out, and_34_out);
  and and_60 (LP, or_6_out, and_35_out);
  and and_61 (PI, and_29_out, and_4_out);
  and and_62 (PO, and_29_out, and_5_out);
  and and_63 (and_63_out, or_8_out, and_14_out);
  or or_14 (EF, and_51_out, or_9_out);
  or or_15 (or_15_out, and_14_out, and_18_out);
  or or_16 (EZ, and_52_out, or_10_out);
  and and_64 (and_64_out, or_11_out, and_4_out);
  and and_65 (and_65_out, or_11_out, and_5_out);
  and and_66 (and_66_out, and_30_out, and_22_out);
  and and_67 (LY, or_5_out, and_41_out);
  and and_68 (and_68_out, and_26_out, and_36_out);
  or or_17 (or_17_out, and_31_out, and_33_out);
  or or_18 (LX, and_39_out, and_63_out);
  or or_19 (or_19_out, RI, RO);
  or or_20 (or_20_out, RI, PI);
  and and_69 (and_69_out, or_17_out, and_25_out);
  and and_70 (and_70_out, and_26_out, or_17_out);
  or or_21 (or_21_out, and_63_out, and_38_out);
  or or_22 (RI, IS, and_64_out);
  or or_23 (RO, and_50_out, and_65_out);
  or or_24 (AR, RC, or_12_out);
  nor nor_1 (nor_1_out, AR, AS);
  or or_25 (or_25_out, or_15_out, and_66_out);
  or or_26 (or_26_out, EZ, PO);
  nor nor_2 (nor_2_out, AS, or_19_out);
  or or_27 (or_27_out, or_20_out, and_69_out);
  or or_28 (or_28_out, or_27_out, and_70_out);
  and and_71 (and_71_out, or_32_out, not_3_out);
  or or_29 (or_29_out, and_71_out, EF);
  and and_72 (AC, nor_1_out, or_25_out);
  or or_30 (or_30_out, AC, AS);
  or or_31 (or_31_out, RO, or_26_out);
  or or_32 (or_32_out, or_31_out, and_68_out);
  and and_73 (and_73_out, nor_2_out, and_27_out);
  or or_33 (LI, and_73_out, and_19_out);
  or or_34 (or_34_out, and_19_out, and_74_out);
  and and_74 (and_74_out, nor_2_out, and_15_out);
  or or_35 (or_35_out, or_21_out, or_27_out);
  or or_36 (XT, or_28_out, or_29_out);
  or or_37 (LM, or_30_out, or_12_out);
  and and_75 (LR, or_32_out, ~IS);  // AND_Gate
  or or_38 (IC, LG, or_34_out);
  and and_76 (ER, or_35_out, not_11_out);
  not not_11 (not_11_out, EZ);

  assign LF = EF;
  assign MO = IC;
endmodule

// ALU
module Arithmetic_Logic_Unit (
  input  EF,
  input  EZ,
  input  [7:0] O,
  input  [7:0] D,
  input  LX,
  input  C,
  input  LY,
  input  R,
  input  i,
  output [7:0] D_2
);

  wire Adc___Sbb_o, and_1_out, and_2_out, and_3_out, and_4_out, and_5_out, and_6_out, and_7_out, or_1_out,
       or_2_out, Right_Shift_o;
  wire [3:0] or_3_out;
  wire [7:0] Adc___Sbb_s, Bitwise_AND_s, Bitwise_NOR_s, Bitwise_OR_s, Decoder_d, Enable_s, Reg_X_q, Reg_Y_q,
       Right_Shift_s;

  Multiplexor Enable (.A({8{1'b0}}), .B(O), .S(Enable_s), .M(O[7]));
  and and_1 (and_1_out, C, LX);
  and and_2 (and_2_out, C, LY);
  and and_3 (and_3_out, Enable_s[4], Enable_s[6]);
  Decoder Decoder (.C(Enable_s[6:4]), .E(EZ), .D(Decoder_d));
  D_Latch Reg_X (.D(D), .R(R), .E(and_1_out), .Q(Reg_X_q));
  D_Latch Reg_Y (.D(D), .R(R), .E(and_2_out), .Q(Reg_Y_q));
  and and_4 (and_4_out, and_3_out, ~Enable_s[5]);  // AND_Gate
  and and_5 (and_5_out, Enable_s[5], Enable_s[6]);
  // Probe on Reg_X_q
  // Probe on Reg_Y_q
  BitAnd Bitwise_AND (.A(Reg_X_q), .B(Reg_Y_q), .S(Bitwise_AND_s));
  BitOr Bitwise_OR (.A(Reg_X_q), .B(Reg_Y_q), .S(Bitwise_OR_s));
  BitNor Bitwise_NOR (.A(Reg_X_q), .B(Reg_Y_q), .S(Bitwise_NOR_s));
  RightShift Right_Shift (.A(Reg_X_q), .i(i), .o(Right_Shift_o), .S(Right_Shift_s));
  AdcSbb Adc___Sbb (.M(Decoder_d[7]), .i(i), .A(Reg_X_q), .B(Reg_Y_q), .S(Adc___Sbb_s), .o(Adc___Sbb_o));
  and and_6 (and_6_out, Right_Shift_o, and_4_out);
  and and_7 (and_7_out, Adc___Sbb_o, and_5_out);
  Comparator Comparator (.A(Reg_X_q), .B(Reg_Y_q), .A_B(or_3_out[1]), .A_B_2(or_3_out[2]), .A_B_3(or_3_out[3]));
  or or_1 (or_1_out, EF, Decoder_d[1]);
  assign D_2 = Decoder_d[0] ? Reg_X_q : 8'bz;  // Controlled_Buffer controlled_buffer_1
  assign D_2 = Decoder_d[2] ? Bitwise_AND_s : 8'bz;  // Controlled_Buffer controlled_buffer_2
  assign D_2 = Decoder_d[3] ? Bitwise_OR_s : 8'bz;  // Controlled_Buffer controlled_buffer_3
  assign D_2 = Decoder_d[4] ? Bitwise_NOR_s : 8'bz;  // Controlled_Buffer controlled_buffer_4
  assign D_2 = Decoder_d[5] ? Right_Shift_s : 8'bz;  // Controlled_Buffer controlled_buffer_5
  or or_2 (or_2_out, Decoder_d[6], Decoder_d[7]);
  assign D_2 = or_2_out ? Adc___Sbb_s : 8'bz;  // Controlled_Buffer controlled_buffer_6
  or or_3 (or_3_out[0], and_6_out, and_7_out);
  assign D_2 = or_1_out ? {4'b0000, or_3_out} : 8'bz;  // Controlled_Buffer controlled_buffer_7

  // Notes on the sheet:
  //   Arithmetic Logic Unit
endmodule

// GPR
module General_Purpose_Registers (
  input  LF,
  input  LG,
  input  [7:0] D,
  input  LH,
  input  R,
  input  [7:0] O,
  input  C,
  input  LR,
  input  ER,
  input  AR,
  output [7:0] D_2,
  output i,
  output [15:0] A
);

  wire and_1_out, and_2_out, and_3_out, and_4_out, or_1_out, or_2_out, or_3_out;
  wire [7:0] Input_d, Output_d, Reg_A_q, Reg_B_q, Reg_C_q, Reg_D_q, Reg_E_q, Reg_G_q, Reg_H_q;
  wire [7:1] Reg_F_q;

  Decoder Input (.C(O[2:0]), .E(and_1_out), .D(Input_d));
  and and_1 (and_1_out, C, LR);
  Decoder Output (.C(O[2:0]), .E(ER), .D(Output_d));
  assign D_2 = Output_d[0] ? Reg_A_q : 8'bz;  // Controlled_Buffer controlled_buffer_1
  D_Latch Reg_A (.D(D), .R(R), .E(Input_d[0]), .Q(Reg_A_q));
  D_Latch Reg_B (.D(D), .R(R), .E(Input_d[1]), .Q(Reg_B_q));
  assign D_2 = Output_d[1] ? Reg_B_q : 8'bz;  // Controlled_Buffer controlled_buffer_2
  assign D_2 = Output_d[2] ? Reg_C_q : 8'bz;  // Controlled_Buffer controlled_buffer_3
  D_Latch Reg_C (.D(D), .R(R), .E(Input_d[2]), .Q(Reg_C_q));
  assign D_2 = Output_d[3] ? Reg_D_q : 8'bz;  // Controlled_Buffer controlled_buffer_4
  D_Latch Reg_D (.D(D), .R(R), .E(Input_d[3]), .Q(Reg_D_q));
  and and_2 (and_2_out, C, LF);
  and and_3 (and_3_out, C, LG);
  and and_4 (and_4_out, C, LH);
  or or_1 (or_1_out, and_2_out, Input_d[5]);
  or or_2 (or_2_out, and_3_out, Input_d[6]);
  or or_3 (or_3_out, and_4_out, Input_d[7]);
  D_Latch Reg_E (.D(D), .R(R), .E(Input_d[4]), .Q(Reg_E_q));
  D_Latch Reg_F (.D(D), .R(R), .E(or_1_out), .Q({Reg_F_q, i}));
  D_Latch Reg_G (.D(D), .R(R), .E(or_2_out), .Q(Reg_G_q));
  D_Latch Reg_H (.D(D), .R(R), .E(or_3_out), .Q(Reg_H_q));
  assign D_2 = Output_d[4] ? Reg_E_q : 8'bz;  // Controlled_Buffer controlled_buffer_5
  assign D_2 = Output_d[5] ? {Reg_F_q, i} : 8'bz;  // Controlled_Buffer controlled_buffer_6
  assign D_2 = Output_d[6] ? Reg_G_q : 8'bz;  // Controlled_Buffer controlled_buffer_7
  assign D_2 = Output_d[7] ? Reg_H_q : 8'bz;  // Controlled_Buffer controlled_buffer_8
  assign A = AR ? {Reg_H_q, Reg_G_q} : 16'bz;  // Controlled_Buffer controlled_buffer_9
endmodule

// PC
module Program_Counter (
  input  LC,
  input  SE,
  input  RC,
  input  C,
  input  R,
  input  IC,
  input  [7:0] D,
  input  EC,
  input  AC,
  input  [15:0] A,
  output [7:0] D_2,
  output [15:0] A_2,
  output COF
);

  wire and_1_out, and_2_out, Increment_o, nor_1_out, nor_2_out;
  wire [7:0] Addr___Data_2_s, Addr___Data_3_s, Addr___Data_s, High_byte_q, Increment_2_s, Increment_s,
       Low___High_s, Low_byte_q, New___Last_s;

  Multiplexor Addr___Data (.A(A[7:0]), .B(D), .S(Addr___Data_s), .M(and_1_out));
  and and_1 (and_1_out, ~SE, LC);  // AND_Gate
  and and_2 (and_2_out, SE, LC);
  Multiplexor Addr___Data_2 (.A(A[15:8]), .B(D), .S(Addr___Data_2_s), .M(and_2_out));
  nor nor_1 (nor_1_out, and_1_out, RC);
  Multiplexor New___Last (.A(Addr___Data_s), .B(Increment_s), .S(New___Last_s), .M(nor_1_out));
  nor nor_2 (nor_2_out, RC, and_2_out);
  Multiplexor Addr___Data_3 (.A(Addr___Data_2_s), .B(Increment_2_s), .S(Addr___Data_3_s), .M(nor_2_out));
  D_FlipFlop Low_byte (.D(New___Last_s), .R(R), .C(C), .Q(Low_byte_q));
  D_FlipFlop High_byte (.D(Addr___Data_3_s), .R(R), .C(C), .Q(High_byte_q));
  HalfAdder Increment (.i(IC), .A(Low_byte_q), .o(Increment_o), .S(Increment_s));
  HalfAdder Increment_2 (.i(Increment_o), .A(High_byte_q), .o(COF), .S(Increment_2_s));
  // Probe on Increment_s
  Multiplexor Low___High (.A(Low_byte_q), .B(High_byte_q), .S(Low___High_s), .M(SE));
  // Probe on Increment_2_s
  assign D_2 = EC ? Low___High_s : 8'bz;  // Controlled_Buffer controlled_buffer_1
  assign A_2 = AC ? {High_byte_q, Low_byte_q} : 16'bz;  // Controlled_Buffer controlled_buffer_2

  // Notes on the sheet:
  //   Program Counter
endmodule

// SP
module Stack_Pointer (
  input  DS,
  input  IS,
  input  R,
  input  ES,
  input  AS,
  input  LS,
  input  SE,
  input  [7:0] D,
  input  C,
  output [7:0] D_2,
  output [15:0] A,
  output SOF
);

  wire and_1_out, and_2_out, and_3_out, and_4_out, Inc___Dec_o, or_1_out;
  wire [7:0] High_byte_q, Inc___Dec_2_s, Inc___Dec_s, Input_2_s, Input_s, Low_byte_q, Output_s;

  Multiplexor Input (.A(Inc___Dec_s), .B(D), .S(Input_s), .M(and_1_out));
  and and_1 (and_1_out, ~SE, LS);  // AND_Gate
  and and_2 (and_2_out, SE, LS);
  Multiplexor Input_2 (.A(Inc___Dec_2_s), .B(D), .S(Input_2_s), .M(and_2_out));
  or or_1 (or_1_out, IS, DS);
  and and_3 (and_3_out, or_1_out, C);
  and and_4 (and_4_out, Inc___Dec_o, and_3_out);
  D_FlipFlop Low_byte (.D(Input_s), .R(R), .C(and_3_out), .Q(Low_byte_q));
  D_FlipFlop High_byte (.D(Input_2_s), .R(R), .C(and_4_out), .Q(High_byte_q));
  IncDec Inc___Dec (.M(DS), .o(Inc___Dec_o), .A(Low_byte_q), .S(Inc___Dec_s));
  IncDec Inc___Dec_2 (.M(DS), .o(SOF), .A(High_byte_q), .S(Inc___Dec_2_s));
  Multiplexor Output (.A(Low_byte_q), .B(High_byte_q), .S(Output_s), .M(SE));
  assign D_2 = ES ? Output_s : 8'bz;  // Controlled_Buffer controlled_buffer_1
  assign A = AS ? {High_byte_q, Low_byte_q} : 16'bz;  // Controlled_Buffer controlled_buffer_2
endmodule

// MAR
module Memory_Address_Register (
  input  LM,
  input  C,
  input  R,
  input  [15:0] A,
  output [15:0] A_2
);

  wire and_1_out;

  and and_1 (and_1_out, C, LM);
  D_Latch Low_byte (.D(A[7:0]), .R(R), .E(and_1_out), .Q(A_2[7:0]));
  D_Latch High_byte (.D(A[15:8]), .R(R), .E(and_1_out), .Q(A_2[15:8]));

  // Notes on the sheet:
  //   Memory Address Register
endmodule

// IR
module Instruction_Register (
  input  LI,
  input  C,
  input  R,
  input  [7:0] D,
  output [7:0] O
);

  wire and_1_out;

  and and_1 (and_1_out, C, LI);
  D_Latch Instruction (.D(D), .R(R), .E(and_1_out), .Q(O));

  // Notes on the sheet:
  //   Instruction Register
endmodule

// SC
module Step_Counter (
  input  HLT,
  input  CLK,
  input  INT,
  input  COF,
  input  SOF,
  input  XT,
  input  R,
  output C,
  output [2:0] T
);

  wire nand_1_out, nor_1_out, or_1_out, or_2_out;
  wire [7:0] Increment_s, Next___Reset_s;
  wire [7:3] Step_q;

  or or_1 (or_1_out, HLT, INT);
  or or_2 (or_2_out, COF, SOF);
  nor nor_1 (nor_1_out, or_1_out, or_2_out);
  nand nand_1 (nand_1_out, CLK, nor_1_out);
  Multiplexor Next___Reset (.A(Increment_s), .B({8{1'b0}}), .S(Next___Reset_s), .M(XT));
  not not_1 (C, nand_1_out);
  D_FlipFlop Step (.D(Next___Reset_s), .R(R), .C(nand_1_out), .Q({Step_q, T}));
  HalfAdder Increment (.i(1'b1), .A({Step_q, T}), .S(Increment_s));  // open: o

  // Notes on the sheet:
  //   Step Counter
endmodule

module MEMORY (
  input  R,
  input  RO,
  input  MO,
  input  EB,
  input  RI,
  input  [15:0] A,
  input  [7:0] D,
  input  LB,
  input  SE,
  input  C,
  output [7:0] D_2
);

  wire and_1_out, and_2_out, and_3_out, and_5_out, not_1_out, or_1_out, or_2_out;
  wire [7:0] Execution_Bank_q, Memory_Bank_q, multiplexor_1_s;
  wire [23:23] and_4_out;

  and and_1 (and_1_out, LB, C);
  and and_2 (and_2_out, ~SE, and_1_out);  // AND_Gate
  and and_3 (and_3_out, and_1_out, SE);
  D_Latch Memory_Bank (.D(D), .R(R), .E(and_2_out), .Q(Memory_Bank_q));
  D_Latch Execution_Bank (.D(D), .R(R), .E(and_3_out), .Q(Execution_Bank_q));
  or or_1 (or_1_out, RO, MO);
  assign D = EB ? multiplexor_1_s : 8'bz;  // Controlled_Buffer controlled_buffer_1
  Multiplexor multiplexor_1 (.A(Memory_Bank_q), .B(Execution_Bank_q), .S(multiplexor_1_s), .M(or_2_out));
  or or_2 (or_2_out, MO, SE);
  and and_4 (and_4_out[23], multiplexor_1_s[7], RI);
  and and_5 (and_5_out, RI, C);
  RAM #(.addrWidth(24), .simpleMode("false"), .Select("low")) ram_1 (
    .addr({and_4_out[23], multiplexor_1_s[6:0], A}), .data(D), .sel(not_1_out), .clk(and_5_out),
    .ld(or_1_out), .clr(not_1_out));
  not not_1 (not_1_out, R);

  assign D_2 = D;
endmodule

// PR
module Port_Register (
  input  PI,
  input  PO,
  input  [7:0] D,
  input  R,
  input  C,
  input  LP,
  output SE,
  output EC,
  output ES,
  output EB,
  output LC,
  output LS,
  output LB
);

  wire and_1_out, and_2_out, and_3_out, and_4_out, and_5_out, and_6_out, and_7_out, and_8_out, and_9_out,
       and_10_out, and_11_out, or_1_out;
  wire [7:0] d_latch_1_q;

  and and_1 (and_1_out, C, LP);
  D_Latch d_latch_1 (.D(D), .R(R), .E(and_1_out), .Q(d_latch_1_q));
  and and_2 (and_2_out, ~d_latch_1_q[1], ~d_latch_1_q[2]);  // AND_Gate
  and and_3 (and_3_out, d_latch_1_q[1], ~d_latch_1_q[2]);  // AND_Gate
  and and_4 (and_4_out, ~d_latch_1_q[1], d_latch_1_q[2]);  // AND_Gate
  and and_5 (and_5_out, ~d_latch_1_q[4], ~d_latch_1_q[5]);  // AND_Gate
  and and_6 (and_6_out, ~d_latch_1_q[6], ~d_latch_1_q[7]);  // AND_Gate
  and and_7 (and_7_out, ~d_latch_1_q[3], and_8_out);  // AND_Gate
  and and_8 (and_8_out, and_5_out, and_6_out);
  and and_9 (and_9_out, and_2_out, and_7_out);
  and and_10 (and_10_out, and_3_out, and_7_out);
  and and_11 (and_11_out, and_4_out, and_7_out);
  or or_1 (or_1_out, PO, PI);
  and and_12 (SE, or_1_out, d_latch_1_q[0]);
  and and_13 (EC, and_9_out, PO);
  and and_14 (ES, and_10_out, PO);
  and and_15 (EB, and_11_out, PO);
  and and_16 (LC, and_9_out, PI);
  and and_17 (LS, and_10_out, PI);
  and and_18 (LB, and_11_out, PI);
endmodule
